// Logisim project Practica 3.circ as structural Verilog: 1 circuit, main circuit main
module main (
  input  W,
  input  X,
  input  X_2,
  input  Y,
  input  Y_2,
  input  Z,
  input  Z_2,
  input  in_8,
  input  in_9,
  output out_10,
  output out_11,
  output out_12
);

  wire and_1_out, and_2_out, and_3_out, and_4_out, and_5_out, not_1_out, not_2_out;

  not not_1 (not_1_out, X_2);
  not not_2 (not_2_out, Y_2);
  and and_1 (and_1_out, W, X_2);
  and and_2 (and_2_out, not_1_out, not_2_out, Z);
  xnor xnor_1 (out_12, in_8, in_9);
  or or_1 (out_10, and_1_out, and_2_out);
  and and_3 (and_3_out, X, Y);
  and and_4 (and_4_out, Y, Z_2, Z_2);
  and and_5 (and_5_out, X, Z_2);
  or or_2 (out_11, and_3_out, and_4_out, and_5_out);

  // Notes on the sheet:
  //   Inciso 1: Reducción
  //   Inciso 3: Compuerta
  //   Inciso 2: El club de Tobi
endmodule
